// Logisim project 5-bit Magnitude Comparator.circ as structural Verilog: 1 circuit, main circuit main
module main (
  input  A4,
  input  B4,
  input  A3,
  input  B3,
  input  A2,
  input  B2,
  input  A1,
  input  B1,
  input  A0,
  input  B0,
  output A___B,
  output A___B_2,
  output A___B_3
);

  wire and_1_out, and_2_out, and_3_out, and_4_out, and_5_out, and_6_out, and_7_out, and_8_out, and_9_out,
       and_10_out, and_11_out, and_12_out, and_13_out, and_14_out, and_15_out, and_16_out, and_17_out,
       and_18_out, not_1_out, not_2_out, not_3_out, not_4_out, not_5_out, not_6_out, not_7_out, not_8_out,
       not_9_out, not_10_out, X0_out, X1_out, X2_out, X3_out, X4_out;

  not not_1 (not_1_out, A4);
  not not_2 (not_2_out, B4);
  not not_3 (not_3_out, A3);
  not not_4 (not_4_out, B3);
  not not_5 (not_5_out, A2);
  not not_6 (not_6_out, B2);
  not not_7 (not_7_out, A1);
  not not_8 (not_8_out, B1);
  not not_9 (not_9_out, A0);
  not not_10 (not_10_out, B0);
  and and_1 (and_1_out, not_1_out, B4);
  and and_2 (and_2_out, A4, not_2_out);
  and and_3 (and_3_out, not_3_out, B3);
  and and_4 (and_4_out, A3, not_4_out);
  and and_5 (and_5_out, not_5_out, B2);
  and and_6 (and_6_out, A2, not_6_out);
  and and_7 (and_7_out, not_7_out, B1);
  and and_8 (and_8_out, A1, not_8_out);
  and and_9 (and_9_out, not_9_out, B0);
  and and_10 (and_10_out, A0, not_10_out);
  nor X4 (X4_out, and_1_out, and_2_out);
  nor X3 (X3_out, and_3_out, and_4_out);
  nor X2 (X2_out, and_5_out, and_6_out);
  nor X1 (X1_out, and_7_out, and_8_out);
  nor X0 (X0_out, and_9_out, and_10_out);
  and and_11 (and_11_out, X4_out, and_3_out);
  and and_12 (and_12_out, X4_out, and_4_out);
  and and_13 (and_13_out, X4_out, X3_out, and_5_out);
  and and_14 (and_14_out, X4_out, X3_out, and_6_out);
  and and_15 (and_15_out, X4_out, X3_out, X2_out, and_7_out);
  and and_16 (and_16_out, X4_out, X3_out, X2_out, and_8_out);
  and and_17 (and_17_out, X4_out, X3_out, X2_out, X1_out, and_9_out);
  and and_18 (and_18_out, X4_out, X3_out, X2_out, X1_out, and_10_out);
  and and_19 (A___B_3, X4_out, X3_out, X2_out, X1_out, X0_out);
  or u_A___B (A___B, and_1_out, and_11_out, and_13_out, and_15_out, and_17_out);
  or u_A___B_2 (A___B_2, and_2_out, and_12_out, and_14_out, and_16_out, and_18_out);

  // Notes on the sheet:
  //   Comparison of two binary number A and B
  //   CIRCUIT IMPLEMENTATION OF 5-BIT MAGNITUDE COMPARATOR
endmodule
